# Fritzing sketch breadboard-shift-register (saved by Fritzing 0.9.3b)
breadboards: 1

parts:
  Part1 = Adafruit Metro M0 Express
  U1 = 74HC595 [package="DIP16 [THT]"]
  U2 = 74HC595 [package="DIP16 [THT]"]
  LED2 = smd LED [color="Red (633nm)" package="0603 [SMD]"]
  R2 = Resistor [tolerance=±5% resistance=470k package=THT]
  U3 = 74HC165 [part_number=SN74LS165 package="DIP16 [THT]"]

nets:
  N1: Part1.MISO, U3.Q2
  N2: Part1.SCK, U1.SH_CP, U2.SH_CP
  N3: Part1.MOSI, U1.DS
  GND: Part1.GND, U1.GND, U1.OE, U2.GND, U2.OE, R2.Pin_1, U3.GND
  N4: Part1.D12, U1.ST_CP, U2.ST_CP
  3.3V: Part1.3.3V, U1.MR, U1.VCC, U2.MR, U2.VCC, U3.VCC
  N5: U1.Q1, LED2.anode
  N6: U1.Q7', U2.DS
  N7: LED2.cathode, R2.Pin_0

custom parts:
  Adafruit Metro M0 Express: Metro is our series of microcontroller boards for use with the Arduino IDE. This new Metro board looks a whole lot like our original Metro 328, but with a huge upgrade. Instead of the ATmega328, this Metro features a ATSAMD21G18 chip, an ARM Cortex M0+. It's our first Metro that is designed for use with CircuitPython! CircuitPython is our beginner-oriented flavor of MicroPython - and as the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
  74HC165: 8-bit parallel-load shift registers
