# Fritzing sketch perf-shift-register (saved by Fritzing 0.9.3b)

parts:
  Part1 = Adafruit Metro M0 Express
  U1 = 74HC595 [package="DIP16 [THT]"]
  Part2 = EasyDriver_v44 [part_number=TB6600]
  U2 = 74HC165 [part_number=SN74LS165 package="DIP16 [THT]"]
  S1 = Round Pushbutton [part_number=Limit1]
  Part3 = EasyDriver_v44 [part_number=TB6600]
  S2 = Round Pushbutton [part_number=Limit1]
  R3 = Vertical Resistor [tolerance=±5% resistance=1k package=THT]
  U9 = RJ45 Jack [part_number=actualrj45 package=rj45-8]
  U11 = RJ45 Jack [package=rj45-8]
  U12 = RJ45 Jack [package=rj45-8]
  U13 = RJ45 Jack [part_number=actualrj45 package=rj45-8]
  J1 = Camdenboss CTB0158-12 [part_number=CTB0158-12 package=THT]
  J2 = Camdenboss CTB0158-12 [part_number=CTB0158-12 package=THT]
  JP3 = Header 1 [package=1x01_offset]
  JP4 = Header 1 [package=1x01_offset]
  JP6 = Header 1 [package=1x01_offset]
  JP7 = Header 1 [package=1x01_offset]
  JP8 = Header 1 [package=1x01_offset]
  JP9 = Header 1 [package=1x01_offset]
  JP11 = Header 1 [package=1x01_offset]
  JP13 = Header 1 [package=1x01_offset]
  JP14 = Header 1 [package=1x01_offset]
  JP15 = Header 1 [package=1x01_offset]
  JP16 = Header 1 [package=1x01_offset]
  JP17 = Header 1 [package=1x01_offset]
  JP18 = Header 1 [package=1x01_offset]
  JP20 = Header 1 [package=1x01_offset]  # not connected
  JP23 = Header 1 [package=1x01_offset]
  JP24 = Header 1 [package=1x01_offset]
  JP25 = Header 1 [package=1x01_offset]
  JP26 = Header 1 [package=1x01_offset]
  JP27 = Header 1 [package=1x01_offset]
  JP32 = Header 1 [package=1x01_offset]
  JP33 = Header 1 [package=1x01_offset]
  JP34 = Header 1 [package=1x01_offset]
  JP35 = Header 1 [package=1x01_offset]
  JP36 = Header 1 [package=1x01_offset]
  JP37 = Header 1 [package=1x01_offset]
  JP38 = Header 1 [package=1x01_offset]
  JP39 = Header 1 [package=1x01_offset]
  JP40 = Header 1 [package=1x01_offset]
  JP41 = Header 1 [package=1x01_offset]
  JP42 = Header 1 [package=1x01_offset]
  JP43 = Header 1 [package=1x01_offset]
  JP44 = Header 1 [package=1x01_offset]
  JP45 = Header 1 [package=1x01_offset]  # not connected
  JP46 = Header 1 [package=1x01_offset]
  JP47 = Header 1 [package=1x01_offset]
  JP48 = Header 1 [package=1x01_offset]
  R4 = Resistor [tolerance=±5% resistance=1k package=THT]
  R5 = Resistor [tolerance=±5% resistance=1k package=THT]
  R6 = Resistor [tolerance=±5% resistance=1k package=THT]
  R7 = Resistor [tolerance=±5% resistance=1k package=THT]
  JP49 = Header 1 [package=1x01_offset]
  JP50 = Header 1 [package=1x01_offset]

nets:
  LOW: Part1.A4
  FakeLimitSwitches: Part1.A5
  MISO: Part1.MISO, U2.Q7', U11.8, JP46.1
  CLK: Part1.SCK, U1.SH_CP, U2.Q2, U9.6, U11.7, JP18.1, JP42.1, JP43.1, JP44.1
  MOSI: Part1.MOSI, U1.DS, U11.5, JP17.1
  GND: Part1.GND, U1.GND, U1.OE, Part2.GND, U2.GND, U2.Q0, S1.leg1, Part3.GND, S2.leg1, R3.Pin_1, U12.7, U13.6, J1.pin2, JP4.1, JP15.1, JP16.1, JP26.1, JP27.1, JP32.1, JP33.1
  LATCH: Part1.D12, U1.ST_CP, U9.7, U11.6, JP11.1, JP39.1, JP40.1, JP41.1
  SH/LD: Part1.D11, U2.Q1, U12.5, U13.8, JP47.1, JP48.1, JP49.1, JP50.1
  EN: Part1.D10, Part2.ENABLE, Part3.ENABLE, R3.Pin_0, U12.6, U13.7, J2.pin3, JP34.1, JP35.1, JP36.1
  3.3V: Part1.3.3V, U1.MR, U1.VCC, Part2.VCC, U2.VCC, Part3.VCC, U12.8, U13.5, J1.pin1, JP7.1, JP8.1, JP9.1, JP13.1, JP14.1, JP23.1, JP24.1, JP25.1, R4.Pin_1, R5.Pin_1, R6.Pin_1, R7.Pin_1
  N1: U1.Q1, Part2.STEP, J1.pin4
  N2: U1.Q2, Part3.DIR, J1.pin6
  N3: U1.Q3, Part3.SLEEP, J1.pin7
  N4: U1.Q4, J1.pin9
  N5: U1.Q5, J1.pin10
  N6: U1.Q6, J1.pin12
  N7: U1.Q7, J2.pin1
  N8: U1.Q7', U9.8, JP37.1, JP38.1
  N9: U1.Q0, Part2.DIR, J1.pin3
  24V: Part2.V+, Part3.V+
  Limit2: U2.Q3, J1.pin11, R6.Pin_0
  Limit3: U2.Q5, J2.pin2, R7.Pin_0
  SER in: U2.MR, U9.5, JP3.1, JP6.1
  Limit0: U2.SH_CP, S1.leg0, J1.pin5, R4.Pin_0
  Limit1: U2.OE, S2.leg0, J1.pin8, R5.Pin_0

notes:
  add header oles
  can swap 2&15
  White - bridge
  grey - lead
  EN
  shield GND
  All RJ45 Change:
  short pairs together
  15 terminals
  at 0.2 spacing
  3"!

custom parts:
  Adafruit Metro M0 Express: Metro is our series of microcontroller boards for use with the Arduino IDE. This new Metro board looks a whole lot like our original Metro 328, but with a huge upgrade. Instead of the ATmega328, this Metro features a ATSAMD21G18 chip, an ARM Cortex M0+. It's our first Metro that is designed for use with CircuitPython! CircuitPython is our beginner-oriented flavor of MicroPython - and as the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
  74HC165: 8-bit parallel-load shift registers
  Vertical Resistor: A generic resistor (0.25W)
