# Fritzing sketch wiring-layout (saved by Fritzing 0.9.3b)

parts:
  U1 = 74HC165 [part_number=SN74LS165 package="DIP16 [THT]"]
  U2 = 74HC595 [package="DIP16 [THT]"]
  M1 = Stepper Motor - Bipolar
  Part1 = EasyDriver_v44 [part_number=TB6600]
  S1 = Pushbutton [part_number=limit package="[THT]"]
  Part2 = Adafruit Metro M0 Express
  U3 = Header 8 [part_number="2x10 Ribmale" package=1x08_smd]  # not connected
  M2 = Stepper Motor - Bipolar
  Part3 = EasyDriver_v44 [part_number=TB6600]
  S2 = Pushbutton [part_number=limit package="[THT]"]
  R1 = Resistor [tolerance=±5% resistance=10k package="1206 [SMD]"]
  R2 = Resistor [tolerance=±5% resistance=10k package="1206 [SMD]"]
  Part4 = Adafruit LM3671 Buck Converter [part_number="24V Supply"]
  U4 = Header 8 [part_number="2x10 Ribfemale" package=1x08_smd]  # not connected
  U5 = Header 8 [part_number="2x10 Ribfemale" package=1x08_smd]  # not connected
  U6 = Header 8 [part_number="2x10 Ribfemale" package=1x08_smd]  # not connected
  U7 = Header 8 [part_number="2x10 Ribfemale" package=1x08_smd]  # not connected
  U8 = Header 5x2 [part_number="2x8 dip socket" package=2x5-ra]  # not connected
  U9 = Header 5x2 [part_number="2x8 dip socket" package=2x5-ra]  # not connected

nets:
  N1: U1.Q1, U2.ST_CP, Part2.D12
  N2: U1.Q2, U2.SH_CP, Part2.SCK
  GND: U1.GND, U1.Q0, U2.GND, U2.OE, Part1.GND, S1.Pin_3, S1.Pin_4, Part2.GND, Part3.GND, S2.Pin_4, Part4.GND
  N3: U1.MR, Part2.MISO
  N4: U1.SH_CP, S1.Pin_1, S1.Pin_2, R1.Pin_0
  N5: U1.ST_CP, S2.Pin_1, S2.Pin_2, R2.Pin_0
  VCC: U1.VCC, U2.MR, U2.VCC, Part1.VCC, Part2.3.3V, Part3.VCC, R1.Pin_1, R2.Pin_1
  N6: U2.Q1, Part1.STEP
  N7: U2.Q2, Part3.STEP
  N8: U2.Q3, Part3.DIR
  N9: U2.DS, Part2.MOSI
  N10: U2.Q0, Part1.DIR
  N11: M1.A, Part1.OUT2A
  N12: M1.C, Part1.OUT2B
  N13: M1.B, Part1.OUT1A
  N14: M1.D, Part1.OUT1B
  N15: Part1.V+, Part3.V+, Part4.3.3V
  N16: M2.A, Part3.OUT2A
  N17: M2.C, Part3.OUT2B
  N18: M2.B, Part3.OUT1A
  N19: M2.D, Part3.OUT1B

notes:
  supports 5
  steppers
  3M 905 bulk
  10 conductor
  shielded
  Cleft
  Wiring Plan
  Rib(fem)ale
  are press/crimp
  ribbon connectors
  2x10

custom parts:
  74HC165: 8-bit parallel-load shift registers
  Adafruit Metro M0 Express: Metro is our series of microcontroller boards for use with the Arduino IDE. This new Metro board looks a whole lot like our original Metro 328, but with a huge upgrade. Instead of the ATmega328, this Metro features a ATSAMD21G18 chip, an ARM Cortex M0+. It's our first Metro that is designed for use with CircuitPython! CircuitPython is our beginner-oriented flavor of MicroPython - and as the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
  Adafruit LM3671 Buck Converter: Your power supply problems just got SUPER SOLVED! This 3.3V Buck Converter Breakout board is great for supplying power to low voltage circuits from a single Li-Ion cell battery or USB power. This chip provides up to 600-mA load current across the entire input voltage range of 3.5 to 5.5V. Great for your portable project, we made this "pin compatible" with the LM1117-3.3V TO-220 chip so you can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
